# Fritzing sketch IRRxTx (saved by Fritzing 0.9.0b)
circuit board: 8.46667cm x 5.64444cm
breadboards: 1

parts:
  Red_LED = LED - 5mm [color="Red (633nm)" package="5 mm [THT]"]
  Green_LED = LED - 5mm [color="Green (565nm)" package="5 mm [THT]"]
  NPN_Transistor = NPN-Transistor [package="TO92 [THT]"]
  IR_Tx2 = LED - 5mm [color="Infrared (850nm)" package="5 mm [THT]"]
  IR_Receiver = Infrared Proximity Sensor
  IR_RxTx_Shield = Arduino Uno (Rev3)
  1K_ohm = Resistor [tolerance=±5% resistance=1 package=THT]
  Fire_Cannon = Pushbutton [package="[THT]"]
  R1 = Resistor [tolerance=±5% resistance=220 package=THT]
  Fire_Machine_Gun = Pushbutton [package="[THT]"]
  R2 = Resistor [tolerance=±5% resistance=220 package=THT]
  R3 = Resistor [tolerance=±5% resistance=220 package=THT]
  IR_Tx1 = LED - 5mm [color="Red (633nm)" package="5 mm [THT]"]
  R4 = Resistor [tolerance=±5% resistance=220 package=THT]

nets:
  GND: Red_LED.cathode, Green_LED.cathode, NPN_Transistor.E, IR_Receiver.GND, IR_RxTx_Shield.GND, Fire_Cannon.Pin_1, Fire_Cannon.Pin_2, Fire_Machine_Gun.Pin_3, Fire_Machine_Gun.Pin_4
  N1: Red_LED.anode, R2.Pin_1
  N2: Green_LED.anode, R3.Pin_1
  N3: NPN_Transistor.B, 1K_ohm.Pin_1
  N4: NPN_Transistor.C, IR_Tx1.cathode
  N5: IR_Tx2.cathode, IR_Tx1.anode
  N6: IR_Tx2.anode, R4.Pin_0
  N7: IR_Receiver.Vout, IR_RxTx_Shield.D10_PWM/SS
  N8: IR_Receiver.Vcc, R1.Pin_0
  N9: IR_RxTx_Shield.D8, Fire_Machine_Gun.Pin_1, Fire_Machine_Gun.Pin_2
  N10: IR_RxTx_Shield.D9_PWM, Fire_Cannon.Pin_3, Fire_Cannon.Pin_4
  N11: IR_RxTx_Shield.D11_PWM/MOSI, R3.Pin_0
  N12: IR_RxTx_Shield.D12/MISO, R2.Pin_0
  N13: IR_RxTx_Shield.D3_PWM, 1K_ohm.Pin_0
  N14: IR_RxTx_Shield.3V3, R4.Pin_1
  N15: IR_RxTx_Shield.5V, R1.Pin_1
